// Logisim project 16bit CPU by KCAL2845.circ as structural Verilog: 19 circuits, main circuit CPU
module main (
);

  wire C_out, clock_1_out, cpu_1_ram, EN_out, \i_o_컨트롤러_1_clear , \i_o_컨트롤러_1_clk , \i_o_컨트롤러_1_en ,
       \i_o_컨트롤러_1_load_2 , \i_o_컨트롤러_1_tty_clk , not_1_out, \데이터_버스_1_i_o_load , \데이터_버스_1_ram_load ;
  wire [3:0] \i_o_컨트롤러_1_counter ;
  wire [6:0] \i_o_컨트롤러_1_tty_out , keyboard_1_data;
  wire [9:0] cpu_1_address;
  wire [15:0] cpu_1_out_4, cpu_1_out_6, \i_o_컨트롤러_1_out , ram_1_data, \데이터_버스_1_i_o_2 , \데이터_버스_1_ram_2 ,
       \데이터_버스_1_to_cpu ;

  Clock clock_1 (.out(clock_1_out));
  not not_1 (not_1_out, \데이터_버스_1_ram_load );
  RAM #(.addrWidth(10), .dataWidth(16)) ram_1 (
    .addr(cpu_1_address), .data(ram_1_data), .clk(clock_1_out), .ld(not_1_out));  // open: sel, clr
  Hex_Digit_Display hex_digit_display_1 (.value(\i_o_컨트롤러_1_counter ));  // open: dp
  assign ram_1_data = \데이터_버스_1_ram_load  ? \데이터_버스_1_ram_2  : 16'bz;  // Controlled_Buffer controlled_buffer_1
  TTY #(.rows(4), .trigger("falling")) tty_1 (
    .data(\i_o_컨트롤러_1_tty_out ), .clk(\i_o_컨트롤러_1_tty_clk ), .we(\i_o_컨트롤러_1_load_2 ),
    .clr(\i_o_컨트롤러_1_clear ));
  Keyboard #(.trigger("falling")) keyboard_1 (
    .clk(\i_o_컨트롤러_1_clk ), .re(\i_o_컨트롤러_1_en ), .clr(C_out), .data(keyboard_1_data));  // open: avail
  \데이터_버스  \u_데이터_버스_1  (
    .\RAM_제어 (cpu_1_ram), .Address(cpu_1_address), .RAM(ram_1_data), .I_O(\i_o_컨트롤러_1_out ),
    .RAM_2(\데이터_버스_1_ram_2 ), .I_O_2(\데이터_버스_1_i_o_2 ), .RAM_Load(\데이터_버스_1_ram_load ),
    .I_O_Load(\데이터_버스_1_i_o_load ), .To_CPU(\데이터_버스_1_to_cpu ), .From_CPU(cpu_1_out_4));
  CPU cpu_1 (
    .Address(cpu_1_address), .RAM(cpu_1_ram), .in_1(\데이터_버스_1_to_cpu ), .out_4(cpu_1_out_4),
    .in_2(clock_1_out), .out_6(cpu_1_out_6));
  // Probe on cpu_1_out_6
  \I_O_컨트롤러  \i_o_컨트롤러_1  (
    .keyboard_input(keyboard_1_data), .clk(\i_o_컨트롤러_1_clk ), .En(\i_o_컨트롤러_1_en ), .button_status(EN_out),
    .Address(cpu_1_address), .out(\i_o_컨트롤러_1_out ), .in_4(clock_1_out), .in(\데이터_버스_1_i_o_2 ),
    .TTY_out(\i_o_컨트롤러_1_tty_out ), .clear(\i_o_컨트롤러_1_clear ), .load_2(\i_o_컨트롤러_1_load_2 ),
    .tty_clk(\i_o_컨트롤러_1_tty_clk ), .Counter(\i_o_컨트롤러_1_counter ), .Load(\데이터_버스_1_i_o_load ));  // open: LED
  Button EN (.out(EN_out));
  Button C (.out(C_out));

  // Notes on the sheet:
  //   메모리
  //   시리얼 모니터 & 키보드
endmodule

module CPU (
  input  [15:0] in_1,
  input  in_2,
  output [9:0] Address,
  output [15:0] out_4,
  output RAM,
  output [15:0] out_6
);

  wire ACL, CMP, CMPL, cu_1_ar_l, cu_1_ir_l, cu_1_ir_o, DRI, DRL, PC_plus_plus, PCL, SFL, STL;
  wire [2:0] cu_1_bus, cu_1_out_4;
  wire [3:0] \alu_1_플래그 , select;
  wire [5:0] ir_1_op;
  wire [7:0] sf_1_sf_out;
  wire [15:0] alu_1_out_5, ar_1_out_4, bus_1_out_8, bus_1_out_9, bus_1_out_10, bus_1_out_11, bus_1_out_12,
       dr_1_out_6, ir_1_out_5, pc_1_out_5, st_1_out_4;

  // Probe on Address
  AR ar_1 (.in_1(bus_1_out_12), .out_4(ar_1_out_4), .in_2(cu_1_ar_l), .in_3(in_2), .out_5(Address));
  // Probe on pc_1_out_5
  PC pc_1 (.in_1(bus_1_out_8), .out_5(pc_1_out_5), .in_3(PCL), .in_4(in_2), .in_2(PC_plus_plus));
  // Probe on cu_1_out_4
  CU cu_1 (
    .in_3(in_2), .AR_L(cu_1_ar_l), .BUS(cu_1_bus), .IR_L(cu_1_ir_l), .DR_L(DRL), .DR_I(DRI), .AC_L(ACL),
    .PC_plus_plus(PC_plus_plus), .RAM(RAM), .OP(ir_1_op), .Select(select), .CMP_L(CMPL), .SF_L(SFL),
    .PC_L(PCL), .SF(sf_1_sf_out), .CMP(CMP), .out_4(cu_1_out_4), .ST_L(STL), .IR_O(cu_1_ir_o));
  IR ir_1 (.in_2(bus_1_out_11), .in_3(cu_1_ir_l), .in_4(in_2), .OP(ir_1_op), .IR_O(cu_1_ir_o), .out_5(ir_1_out_5));
  // Probe on ir_1_out_5
  ST st_1 (.in_1(bus_1_out_10), .out_4(st_1_out_4), .in_2(STL), .in_3(in_2));
  DR dr_1 (.DR(bus_1_out_9), .out_6(dr_1_out_6), .in_4(DRL), .in_5(in_2), .DR_I(DRI), .RAM(in_1), .out_7(out_4));
  // Probe on dr_1_out_6
  BUS bus_1 (
    .in_1(ar_1_out_4), .in_2(ir_1_out_5), .in_3(dr_1_out_6), .in_4(out_6), .in_5(pc_1_out_5),
    .in_6(st_1_out_4), .BUS_SELECT(cu_1_bus), .out_9(bus_1_out_9), .out_10(bus_1_out_10),
    .out_11(bus_1_out_11), .out_8(bus_1_out_8), .out_12(bus_1_out_12));
  SF sf_1 (.clk(in_2), .SF_out(sf_1_sf_out), .\ALU에서_입력_받음 (\alu_1_플래그 ), .CMP(CMP), .CMP_L(CMPL), .SF_L(SFL));
  // Probe on \alu_1_플래그 
  // Probe on alu_1_out_5
  ALU alu_1 (.DR(dr_1_out_6), .AC(out_6), .out_5(alu_1_out_5), .ALU_Select(select), .\플래그 (\alu_1_플래그 ));
  AC ac_1 (.in_1(alu_1_out_5), .out_4(out_6), .in_2(ACL), .in_3(in_2));
  // Probe on out_6

  // Other names for the same wires on the sheet: clk = in_2

  // Notes on the sheet:
  //   메뉴얼(구글 독스) : 
  //   CPU 제작자 : kcal2845 (kcal2845@naver.com) 블로그 : https://kcal2845.blog.me/
endmodule

module AR (
  input  [15:0] in_1,
  input  in_2,
  input  in_3,
  output [15:0] out_4,
  output [9:0] out_5
);

  Register #(.width(10), .trigger("falling")) register_1 (
    .D(in_1[9:0]), .en(in_2), .Q(out_4[9:0]), .clk(in_3));  // open: clr

  assign out_4[15:10] = {6{1'b0}};
  assign out_5 = out_4[9:0];
endmodule

module IR (
  input  IR_O,
  input  [15:0] in_2,
  input  in_3,
  input  in_4,
  output [15:0] out_5,
  output [5:0] OP
);

  wire [9:0] register_1_q;

  Register #(.width(16), .trigger("falling")) register_1 (
    .D(in_2), .en(in_3), .Q({OP, register_1_q}), .clk(in_4));  // open: clr
  Multiplexer #(.width(16)) multiplexer_1 (
    .in0({OP, register_1_q}), .in1({{6{1'b0}}, register_1_q}), .out(out_5), .sel(IR_O));  // open: en
endmodule

module DR (
  input  [15:0] DR,
  input  [15:0] RAM,
  input  DR_I,
  input  in_4,
  input  in_5,
  output [15:0] out_6,
  output [15:0] out_7
);

  wire [15:0] multiplexer_1_out;

  Multiplexer #(.width(16)) multiplexer_1 (.in0(DR), .in1(RAM), .out(multiplexer_1_out), .sel(DR_I));  // open: en
  Register #(.width(16), .trigger("falling")) register_1 (
    .D(multiplexer_1_out), .en(in_4), .Q(out_6), .clk(in_5));  // open: clr

  assign out_7 = out_6;
endmodule

module ALU (
  input  [3:0] ALU_Select,
  input  [15:0] DR,
  input  [15:0] AC,
  output [3:0] \플래그 ,
  output [15:0] out_5
);

  wire [15:0] adder_1_out, and_1_out, divider_1_out, multiplier_1_out, negator_1_out, not_1_out, or_1_out,
       shifter_1_out, shifter_2_out, shifter_3_out, shifter_4_out, shifter_5_out, shifter_6_out,
       subtractor_1_out, xor_1_out;

  // Probe on DR
  // Probe on AC
  Negator #(.width(16)) negator_1 (.in(DR), .out(negator_1_out));
  Adder #(.width(16)) adder_1 (.a(AC), .b(DR), .out(adder_1_out));  // open: cin, cout
  Subtractor #(.width(16)) subtractor_1 (.a(AC), .b(DR), .out(subtractor_1_out));  // open: bin, bout
  Multiplier #(.width(16)) multiplier_1 (.a(AC), .b(DR), .out(multiplier_1_out));  // open: cin, cout
  Divider #(.width(16)) divider_1 (.a(AC), .b(DR), .out(divider_1_out));  // open: upper, rem
  assign not_1_out = ~DR;  // NOT_Gate not_1, 16 bits wide
  assign and_1_out = AC & DR;  // AND_Gate and_1, 16 bits wide
  assign or_1_out = AC | DR;  // OR_Gate or_1, 16 bits wide
  assign xor_1_out = AC ^ DR;  // XOR_Gate xor_1, 16 bits wide
  Shifter #(.width(16), .shift("lr")) shifter_1 (.in(DR), .\dist (4'b0001), .out(shifter_1_out));
  Shifter #(.width(16)) shifter_2 (.in(DR), .\dist (4'b0001), .out(shifter_2_out));
  Shifter #(.width(16), .shift("ar")) shifter_3 (.in(DR), .\dist (4'b0001), .out(shifter_3_out));
  Shifter #(.width(16), .shift("ar")) shifter_4 (.in(DR), .\dist (4'b0001), .out(shifter_4_out));
  Shifter #(.width(16), .shift("rr")) shifter_5 (.in(DR), .\dist (4'b0001), .out(shifter_5_out));
  Shifter #(.width(16), .shift("rl")) shifter_6 (.in(DR), .\dist (4'b0001), .out(shifter_6_out));
  // Probe on subtractor_1_out
  // Probe on out_5
  Multiplexer #(.select(4), .width(16)) multiplexer_1 (
    .in0(DR), .in1(negator_1_out), .in2(adder_1_out), .in3(subtractor_1_out), .in4(multiplier_1_out),
    .in5(divider_1_out), .in6(not_1_out), .in7(and_1_out), .in8(or_1_out), .in9(xor_1_out),
    .in10(shifter_1_out), .in11(shifter_2_out), .in12(shifter_3_out), .in13(shifter_4_out),
    .in14(shifter_5_out), .in15(shifter_6_out), .out(out_5), .sel(ALU_Select));  // open: en
  nor ZF (\플래그 [3], out_5[15], out_5[14], out_5[13], out_5[12], out_5[11], out_5[10], out_5[9], out_5[8], out_5[7], out_5[6], out_5[5], out_5[4], out_5[3], out_5[2], out_5[1], out_5[0]);

  assign \플래그 [2] = out_5[15];

  // Notes on the sheet:
  //   ZF SF CF OF
endmodule

module AC (
  input  [15:0] in_1,
  input  in_2,
  input  in_3,
  output [15:0] out_4
);

  Register #(.width(16), .trigger("falling")) register_1 (.D(in_1), .en(in_2), .Q(out_4), .clk(in_3));  // open: clr
endmodule

module PC (
  input  [15:0] in_1,
  input  in_2,
  input  in_3,
  input  in_4,
  output [15:0] out_5
);

  Counter #(.width(10), .max('h3ff), .trigger("falling")) counter_1 (
    .load(in_3), .D(in_1[9:0]), .count(in_2), .Q(out_5[9:0]), .clk(in_4));  // open: carry, clr

  assign out_5[15:10] = {6{1'b0}};
endmodule

module ST (
  input  [15:0] in_1,
  input  in_2,
  input  in_3,
  output [15:0] out_4
);

  Register #(.width(16), .trigger("falling")) register_1 (.D(in_1), .en(in_2), .Q(out_4), .clk(in_3));  // open: clr
endmodule

module SF (
  input  clk,
  input  SF_L,
  input  [3:0] \ALU에서_입력_받음 ,
  input  CMP,
  input  CMP_L,
  output [7:0] SF_out
);

  D_Flip_Flop #(.trigger("falling")) ZF (
    .clk(clk), .D(\ALU에서_입력_받음 [3]), .Q(SF_out[7]), .en(SF_L));  // open: Qn, preset, reset
  D_Flip_Flop #(.trigger("falling")) SF (
    .clk(clk), .D(\ALU에서_입력_받음 [2]), .Q(SF_out[6]), .en(SF_L));  // open: Qn, preset, reset
  D_Flip_Flop #(.trigger("falling")) OF (
    .clk(clk), .D(\ALU에서_입력_받음 [0]), .Q(SF_out[4]), .en(SF_L));  // open: Qn, preset, reset
  D_Flip_Flop #(.trigger("falling")) CF (
    .clk(clk), .D(\ALU에서_입력_받음 [1]), .Q(SF_out[5]), .en(SF_L));  // open: Qn, preset, reset
  D_Flip_Flop #(.trigger("falling")) d_ff_1 (.Q(SF_out[3]));  // open: clk, D, Qn, preset, en, reset
  D_Flip_Flop #(.trigger("falling")) d_ff_2 (.Q(SF_out[2]));  // open: clk, D, Qn, preset, en, reset
  D_Flip_Flop #(.trigger("falling")) d_ff_3 (.Q(SF_out[1]));  // open: clk, D, Qn, preset, en, reset
  D_Flip_Flop #(.trigger("falling")) u_CMP (.clk(clk), .D(CMP), .Q(SF_out[0]), .en(CMP_L));  // open: Qn, preset, reset
endmodule

module CU (
  input  [7:0] SF,
  input  [5:0] OP,
  input  in_3,
  output [2:0] out_4,
  output CMP,
  output [2:0] BUS,
  output [3:0] Select,
  output AR_L,
  output IR_L,
  output DR_L,
  output DR_I,
  output AC_L,
  output PC_plus_plus,
  output PC_L,
  output ST_L,
  output SF_L,
  output CMP_L,
  output RAM,
  output IR_O
);

  wire _1_IR_out, _2_DR_out, _4_PC_out, _7_15_2_out, _7_15_out, and_1_out, and_2_out, and_3_out, and_4_out,
       and_5_out, and_6_out, and_7_out, and_8_out, and_9_out, and_10_out, and_11_out, and_12_out, and_13_out,
       and_14_out, and_15_out, and_16_out, and_17_out, and_18_out, and_19_out, and_21_out, and_22_out,
       and_25_out, and_26_out, and_27_out, and_28_out, and_29_out, and_30_out, and_31_out, and_32_out,
       and_33_out, and_34_out, and_35_out, and_36_out, and_37_out, and_38_out, and_39_out, and_40_out,
       and_41_out, and_42_out, and_43_out, and_44_out, and_45_out, and_46_out, and_47_out, and_48_out,
       and_49_out, and_50_out, and_51_out, decoder_1_out0, decoder_1_out3, decoder_1_out4, decoder_1_out5,
       decoder_1_out6, decoder_1_out7, decoder_2_out1, decoder_2_out2, decoder_2_out3, decoder_2_out4,
       decoder_2_out5, decoder_2_out6, decoder_2_out7, decoder_2_out8, decoder_2_out9, decoder_2_out10,
       decoder_2_out11, decoder_2_out12, decoder_2_out13, decoder_2_out14, decoder_2_out15, decoder_3_out0,
       decoder_3_out1, decoder_3_out2, decoder_3_out3, decoder_4_out0, decoder_4_out2, decoder_4_out3,
       decoder_4_out4, decoder_4_out5, decoder_4_out6, decoder_5_out1, decoder_5_out2, decoder_5_out4,
       decoder_5_out5, decoder_5_out6, decoder_5_out7, decoder_5_out8, decoder_5_out9, decoder_5_out10,
       decoder_5_out11, decoder_5_out12, decoder_5_out13, decoder_5_out14, decoder_5_out15, decoder_6_out7,
       decoder_7_out1, decoder_7_out7, decoder_7_out8, decoder_7_out9, decoder_7_out10, decoder_7_out11,
       decoder_7_out12, decoder_7_out13, decoder_7_out14, decoder_7_out15, decoder_8_out0, decoder_8_out1,
       decoder_8_out2, decoder_8_out3, not_1_out, not_2_out, not_3_out, not_4_out, not_5_out, not_6_out,
       priority_encoder_2_en_out, xnor_1_out, \조건_검사_결과 ;
  wire [3:0] priority_encoder_2_out;

  Counter #(.width(3), .max('h7)) \u_시퀀스_카운터  (.count(in_3), .Q(out_4), .clk(in_3));  // open: load, D, carry, clr
  Decoder #(.select(3)) decoder_1 (
    .out0(decoder_1_out0), .out1(PC_plus_plus), .out2(IR_L), .out3(decoder_1_out3), .out4(decoder_1_out4),
    .out5(decoder_1_out5), .out6(decoder_1_out6), .out7(decoder_1_out7), .sel(out_4));  // open: en
  Decoder #(.select(4)) decoder_2 (
    .out1(decoder_2_out1), .out2(decoder_2_out2), .out3(decoder_2_out3), .out4(decoder_2_out4),
    .out5(decoder_2_out5), .out6(decoder_2_out6), .out7(decoder_2_out7), .out8(decoder_2_out8),
    .out9(decoder_2_out9), .out10(decoder_2_out10), .out11(decoder_2_out11), .out12(decoder_2_out12),
    .out13(decoder_2_out13), .out14(decoder_2_out14), .out15(decoder_2_out15), .sel(OP[5:2]));  // open: out0, en
  or _7_15 (_7_15_out, decoder_2_out7, decoder_2_out8, decoder_2_out9, decoder_2_out10, decoder_2_out11, decoder_2_out12, decoder_2_out13, decoder_2_out14, decoder_2_out15);
  Decoder #(.select(2)) decoder_3 (
    .out0(decoder_3_out0), .out1(decoder_3_out1), .out2(decoder_3_out2), .out3(decoder_3_out3), .sel(OP[1:0]));  // open: en
  and and_1 (and_1_out, decoder_2_out1, decoder_1_out3);
  and and_2 (and_2_out, decoder_2_out2, decoder_1_out3);
  and and_3 (and_3_out, _7_15_out, decoder_1_out3);
  and and_4 (and_4_out, decoder_2_out1, OP[1], decoder_1_out5);
  and and_5 (and_5_out, decoder_2_out2, OP[1], decoder_1_out5);
  and and_6 (and_6_out, decoder_2_out1, decoder_1_out6);
  and and_7 (and_7_out, decoder_2_out2, decoder_1_out6);
  and and_8 (and_8_out, _7_15_out, decoder_1_out4);
  and and_9 (and_9_out, decoder_2_out1, OP[1], decoder_1_out4);
  and and_10 (and_10_out, decoder_2_out2, OP[1], decoder_1_out4);
  and and_11 (and_11_out, decoder_2_out1, not_1_out, decoder_1_out6);
  not not_1 (not_1_out, OP[0]);
  and and_12 (and_12_out, _7_15_out, decoder_1_out4);
  and and_13 (and_13_out, decoder_2_out1, OP[1], decoder_1_out4);
  and and_14 (and_14_out, decoder_2_out2, OP[1], decoder_1_out4);
  and and_15 (and_15_out, decoder_2_out1, decoder_1_out7);
  and and_16 (and_16_out, _7_15_out, decoder_1_out5);
  and and_17 (and_17_out, decoder_2_out4, decoder_1_out3, \조건_검사_결과 );
  and and_18 (and_18_out, decoder_2_out5, decoder_1_out4, \조건_검사_결과 );
  and and_19 (and_19_out, decoder_2_out6, decoder_1_out3);
  and and_20 (ST_L, decoder_2_out5, decoder_1_out3, \조건_검사_결과 );
  and and_21 (and_21_out, decoder_2_out1, decoder_1_out7);
  and and_22 (and_22_out, _7_15_out, decoder_1_out5);
  and u_CMP_L (CMP_L, decoder_2_out3, decoder_1_out3);
  and and_23 (RAM, decoder_2_out2, decoder_1_out7);
  and and_24 (IR_O, decoder_2_out1, OP[0], decoder_1_out6);
  and and_25 (and_25_out, SF[7], decoder_3_out0);
  and and_26 (and_26_out, SF[6], decoder_3_out1);
  and and_27 (and_27_out, SF[5], decoder_3_out2);
  and and_28 (and_28_out, SF[4], decoder_3_out3);
  xnor xnor_1 (xnor_1_out, SF[0], OP[0]);
  not not_2 (not_2_out, OP[1]);
  or or_1 (CMP, and_25_out, and_26_out, and_27_out, and_28_out);
  or or_2 (\조건_검사_결과 , xnor_1_out, not_2_out);
  or u_AR_L (AR_L, decoder_1_out0, and_1_out, and_2_out, and_3_out, and_4_out, and_5_out);
  or u_DR_L (DR_L, PC_plus_plus, and_6_out, and_7_out, and_8_out, and_9_out, and_10_out);
  or u_DR_I (DR_I, PC_plus_plus, and_11_out, and_12_out, and_13_out, and_14_out);
  or or_3 (AC_L, and_15_out, and_16_out);
  or or_4 (PC_L, and_17_out, and_18_out, and_19_out);
  or or_5 (SF_L, and_21_out, and_22_out);
  Decoder #(.select(3)) decoder_4 (
    .out0(decoder_4_out0), .out2(decoder_4_out2), .out3(decoder_4_out3), .out4(decoder_4_out4),
    .out5(decoder_4_out5), .out6(decoder_4_out6), .sel(out_4));  // open: out1, out7, en
  Decoder #(.select(4)) decoder_5 (
    .out1(decoder_5_out1), .out2(decoder_5_out2), .out4(decoder_5_out4), .out5(decoder_5_out5),
    .out6(decoder_5_out6), .out7(decoder_5_out7), .out8(decoder_5_out8), .out9(decoder_5_out9),
    .out10(decoder_5_out10), .out11(decoder_5_out11), .out12(decoder_5_out12), .out13(decoder_5_out13),
    .out14(decoder_5_out14), .out15(decoder_5_out15), .sel(OP[5:2]));  // open: out0, out3, en
  or _7_15_2 (_7_15_2_out, decoder_5_out7, decoder_5_out8, decoder_5_out9, decoder_5_out10, decoder_5_out11, decoder_5_out12, decoder_5_out13, decoder_5_out14, decoder_5_out15);
  and and_29 (and_29_out, decoder_5_out1, decoder_4_out3);
  and and_30 (and_30_out, decoder_5_out2, decoder_4_out3);
  and and_31 (and_31_out, decoder_5_out4, decoder_4_out3);
  and and_32 (and_32_out, decoder_5_out5, decoder_4_out4);
  and and_33 (and_33_out, _7_15_2_out, decoder_4_out3);
  and and_34 (and_34_out, decoder_5_out1, OP[0], decoder_4_out6);
  and and_35 (and_35_out, decoder_5_out1, decoder_4_out5);
  and and_36 (and_36_out, decoder_5_out1, OP[1], decoder_4_out5);
  and and_37 (and_37_out, decoder_5_out2, OP[1], decoder_4_out5);
  and and_38 (and_38_out, decoder_5_out2, decoder_4_out6);
  and and_39 (and_39_out, decoder_5_out5, decoder_4_out3);
  and and_40 (and_40_out, decoder_5_out6, decoder_4_out3);
  or _1_IR (_1_IR_out, and_29_out, and_30_out, and_31_out, and_32_out, and_33_out, and_34_out);
  or _2_DR (_2_DR_out, decoder_4_out2, and_35_out, and_36_out, and_37_out);
  or _4_PC (_4_PC_out, decoder_4_out0, and_39_out);
  Priority_Encoder priority_encoder_1 (
    .in1(_1_IR_out), .in2(_2_DR_out), .in3(and_38_out), .in4(_4_PC_out), .in5(and_40_out), .out(BUS));  // open: in0, in6, in7, en_in, gs, en_out
  Decoder #(.select(3)) decoder_6 (
    .out7(decoder_6_out7), .sel(out_4));  // open: out0, out1, out2, out3, out4, out5, out6, en
  Decoder #(.select(4)) decoder_7 (
    .out1(decoder_7_out1), .out7(decoder_7_out7), .out8(decoder_7_out8), .out9(decoder_7_out9),
    .out10(decoder_7_out10), .out11(decoder_7_out11), .out12(decoder_7_out12), .out13(decoder_7_out13),
    .out14(decoder_7_out14), .out15(decoder_7_out15), .sel(OP[5:2]));  // open: out0, out2, out3, out4, out5, out6, en
  and and_41 (and_41_out, decoder_7_out1, decoder_6_out7);
  Decoder #(.select(2)) decoder_8 (
    .out0(decoder_8_out0), .out1(decoder_8_out1), .out2(decoder_8_out2), .out3(decoder_8_out3), .sel(OP[1:0]));  // open: en
  and and_42 (and_42_out, decoder_7_out12, decoder_8_out0);
  and and_43 (and_43_out, decoder_8_out1, decoder_7_out12);
  and and_44 (and_44_out, decoder_8_out2, decoder_7_out12);
  and and_45 (and_45_out, decoder_8_out3, decoder_7_out12);
  and and_46 (and_46_out, decoder_7_out13, not_3_out);
  not not_3 (not_3_out, OP[0]);
  and and_47 (and_47_out, decoder_7_out13, OP[0]);
  and and_48 (and_48_out, decoder_7_out14, not_4_out);
  not not_4 (not_4_out, OP[0]);
  and and_49 (and_49_out, decoder_7_out14, OP[0]);
  and and_50 (and_50_out, decoder_7_out15, not_5_out);
  not not_5 (not_5_out, OP[0]);
  and and_51 (and_51_out, decoder_7_out15, OP[0]);
  Priority_Encoder #(.select(4)) priority_encoder_2 (
    .in0(and_41_out), .in1(decoder_7_out7), .in2(decoder_7_out8), .in3(decoder_7_out9),
    .in4(decoder_7_out10), .in5(decoder_7_out11), .in6(and_42_out), .in7(and_43_out), .in8(and_44_out),
    .in9(and_45_out), .in10(and_46_out), .in11(and_47_out), .in12(and_48_out), .in13(and_49_out),
    .in14(and_50_out), .in15(and_51_out), .out(priority_encoder_2_out), .en_out(priority_encoder_2_en_out));  // open: gs, en_in
  assign Select = priority_encoder_2_en_out ? 4'b0000 : 4'bz;  // Controlled_Buffer controlled_buffer_1
  assign Select = not_6_out ? priority_encoder_2_out : 4'bz;  // Controlled_Buffer controlled_buffer_2
  not not_6 (not_6_out, priority_encoder_2_en_out);

  // Other names for the same wires on the sheet: CMP_t = SF[0]

  // Notes on the sheet:
  //   OR0      OR1
  //   ZF SF CF OF
  //   조건검사회로
  //   OR0      OR1
endmodule

module BUS (
  input  [15:0] in_1,
  input  [15:0] in_2,
  input  [15:0] in_3,
  input  [15:0] in_4,
  input  [15:0] in_5,
  input  [15:0] in_6,
  input  [2:0] BUS_SELECT,
  output [15:0] out_8,
  output [15:0] out_9,
  output [15:0] out_10,
  output [15:0] out_11,
  output [15:0] out_12
);

  Multiplexer #(.select(3), .width(16)) multiplexer_1 (
    .in0(in_1), .in1(in_2), .in2(in_3), .in3(in_4), .in4(in_5), .in5(in_6), .out(out_8), .sel(BUS_SELECT));  // open: in6, in7, en

  assign out_9 = out_8;
  assign out_10 = out_8;
  assign out_11 = out_8;
  assign out_12 = out_8;
endmodule

module \데이터_버스  (
  input  \RAM_제어 ,
  input  [9:0] Address,
  input  [15:0] RAM,
  input  [15:0] I_O,
  input  [15:0] From_CPU,
  output RAM_Load,
  output I_O_Load,
  output [15:0] To_CPU,
  output [15:0] RAM_2,
  output [15:0] I_O_2
);

  wire not_1_out;

  Multiplexer #(.width(16)) multiplexer_1 (.in0(RAM), .in1(I_O), .out(To_CPU), .sel(Address[9]));  // open: en
  not not_1 (not_1_out, Address[9]);
  and and_1 (RAM_Load, not_1_out, \RAM_제어 );
  and and_2 (I_O_Load, Address[9], \RAM_제어 );

  assign I_O_2 = From_CPU;
  assign RAM_2 = From_CPU;

  // Notes on the sheet:
  //   0~1kb : ram할당 1kb~2kb : i/o 컨트롤러 할당
endmodule

module \출력_장치  (
  input  [15:0] Data,
  input  CLK,
  input  Load,
  input  [9:0] Address,
  output [15:0] out_5,
  output [15:0] out_6,
  output [15:0] out_7,
  output [15:0] out_8,
  output [15:0] out_9,
  output [15:0] out_10,
  output [15:0] out_11,
  output [15:0] out_12
);

  wire decoder_1_out0, decoder_1_out1, decoder_1_out2, decoder_1_out3, decoder_1_out4, decoder_1_out5,
       decoder_1_out6, decoder_1_out7, Load_out, not_1_out;

  and u_Load (Load_out, Load, Address[9], not_1_out);
  not not_1 (not_1_out, Address[8]);
  Decoder #(.select(4), .disabled(0)) decoder_1 (
    .out0(decoder_1_out0), .out1(decoder_1_out1), .out2(decoder_1_out2), .out3(decoder_1_out3),
    .out4(decoder_1_out4), .out5(decoder_1_out5), .out6(decoder_1_out6), .out7(decoder_1_out7),
    .sel(Address[3:0]), .en(Load_out));  // open: out8, out9, out10, out11, out12, out13, out14, out15
  Register #(.width(16), .trigger("falling")) register_1 (
    .D(Data), .en(decoder_1_out0), .Q(out_5), .clk(CLK));  // open: clr
  Register #(.width(16), .trigger("falling")) register_2 (
    .D(Data), .en(decoder_1_out1), .Q(out_6), .clk(CLK));  // open: clr
  Register #(.width(16), .trigger("falling")) register_3 (
    .D(Data), .en(decoder_1_out2), .Q(out_7), .clk(CLK));  // open: clr
  Register #(.width(16), .trigger("falling")) register_4 (
    .D(Data), .en(decoder_1_out3), .Q(out_8), .clk(CLK));  // open: clr
  Register #(.width(16), .trigger("falling")) register_5 (
    .D(Data), .en(decoder_1_out5), .Q(out_10), .clk(CLK));  // open: clr
  Register #(.width(16), .trigger("falling")) register_6 (
    .D(Data), .en(decoder_1_out4), .Q(out_9), .clk(CLK));  // open: clr
  Register #(.width(16), .trigger("falling")) register_7 (
    .D(Data), .en(decoder_1_out6), .Q(out_11), .clk(CLK));  // open: clr
  Register #(.width(16), .trigger("falling")) register_8 (
    .D(Data), .en(decoder_1_out7), .Q(out_12), .clk(CLK));  // open: clr
endmodule

module \입력_장치  (
  input  in_1,
  input  in_2,
  input  in_3,
  input  in_4,
  input  in_5,
  input  in_6,
  input  in_7,
  input  in_8,
  input  in_9,
  input  in_10,
  input  in_11,
  input  in_12,
  input  in_13,
  input  in_14,
  input  in_15,
  input  in_16,
  input  in_17,
  input  [15:0] in_18,
  output [15:0] out_19
);

  wire or_1_out;

  or or_1 (or_1_out, in_1, in_2, in_3, in_4, in_5, in_6, in_7, in_8, in_10, in_11, in_12, in_13, in_14, in_15, in_16, in_9);
  Register #(.width(16)) register_1 (
    .D({in_16, in_15, in_14, in_13, in_12, in_11, in_10, in_9, in_8, in_7, in_6, in_5, in_4, in_3, in_2, in_1}),
    .en(or_1_out), .Q(out_19), .clk(in_17), .clr(in_18[0]));
endmodule

module TTY_control (
  input  [15:0] in_1,
  input  Load,
  input  [9:0] in_3,
  input  clk,
  output clear,
  output load_2,
  output tty_clk,
  output [15:0] out_8,
  output [15:0] out_9,
  output [15:0] out_10
);

  wire and_1_out, decoder_1_out0, decoder_1_out1, decoder_1_out2, decoder_1_out3, not_1_out, \출력_out ;
  wire [15:2] register_4_q;

  not not_1 (not_1_out, in_3[9]);
  nor \u_출력  (\출력_out , in_3[2], in_3[3], in_3[4], in_3[5], in_3[6], in_3[7], in_3[8], not_1_out, 1'b0);
  Decoder #(.select(2), .disabled(0)) decoder_1 (
    .out0(decoder_1_out0), .out1(decoder_1_out1), .out2(decoder_1_out2), .out3(decoder_1_out3),
    .sel(in_3[1:0]), .en(and_1_out));
  and and_1 (and_1_out, Load, \출력_out );
  Register #(.width(16), .trigger("falling")) register_1 (
    .D(in_1), .en(decoder_1_out0), .Q(out_8), .clk(clk));  // open: clr
  Register #(.width(16), .trigger("falling")) register_2 (
    .D(in_1), .en(decoder_1_out1), .Q(out_9), .clk(clk));  // open: clr
  Register #(.width(16), .trigger("falling")) register_3 (
    .D(in_1), .en(decoder_1_out2), .Q(out_10), .clk(clk));  // open: clr
  nor nor_1 (tty_clk, load_2, clear);
  Register #(.width(16), .trigger("falling")) register_4 (
    .D(in_1), .en(decoder_1_out3), .Q({register_4_q, clear, load_2}), .clk(clk));  // open: clr
endmodule

module \키보드_컨트롤  (
  input  [6:0] in_1,
  input  in_2,
  input  button,
  input  [15:0] in_4,
  input  [9:0] in_5,
  output out_6,
  output out_7,
  output out_8,
  output [15:0] out_9
);

  not not_1 (out_6, out_7);
  or or_1 (out_8, in_2, in_4[1]);
  not not_2 (out_7, in_4[0]);
  Multiplexer #(.width(16)) multiplexer_1 (
    .in0({{9{1'b0}}, in_1}), .in1({{15{1'b0}}, button}), .out(out_9), .sel(in_5[0]));  // open: en
endmodule

module \I_O_컨트롤러  (
  input  [6:0] keyboard_input,
  input  button_status,
  input  [15:0] in,
  input  in_4,
  input  [9:0] Address,
  input  Load,
  output clear,
  output load_2,
  output tty_clk,
  output [3:0] Counter,
  output [7:0] LED,
  output [6:0] TTY_out,
  output clk,
  output En,
  output [15:0] out
);

  wire and_1_out, decoder_1_out0, decoder_1_out1, decoder_1_out2, decoder_1_out3, decoder_1_out5, nor_1_out,
       not_1_out;
  wire [7:0] _201_q;
  wire [8:0] _202_q;
  wire [13:0] _203_q;
  wire [14:0] _205_q;
  wire [15:4] _200_q;

  not not_1 (not_1_out, Address[9]);
  Decoder #(.select(4), .disabled(0)) decoder_1 (
    .out0(decoder_1_out0), .out1(decoder_1_out1), .out2(decoder_1_out2), .out3(decoder_1_out3),
    .out5(decoder_1_out5), .sel(Address[3:0]), .en(and_1_out));  // open: out4, out6, out7, out8, out9, out10, out11, out12, out13, out14, out15
  and and_1 (and_1_out, Load, nor_1_out);
  nor nor_1 (nor_1_out, not_1_out, Address[8], Address[7], Address[6], Address[5], Address[4]);
  Register #(.width(16), .trigger("falling")) _200 (
    .D(in), .en(decoder_1_out0), .Q({_200_q, Counter}), .clk(in_4));  // open: clr
  nor nor_2 (tty_clk, load_2, clear);
  Register #(.width(16), .trigger("falling")) _201 (
    .D(in), .en(decoder_1_out1), .Q({_201_q, LED}), .clk(in_4));  // open: clr
  Register #(.width(16), .trigger("falling")) _202 (
    .D(in), .en(decoder_1_out2), .Q({_202_q, TTY_out}), .clk(in_4));  // open: clr
  Register #(.width(16), .trigger("falling")) _203 (
    .D(in), .en(decoder_1_out3), .Q({_203_q, clear, load_2}), .clk(in_4));  // open: clr
  Multiplexer #(.select(4), .width(16)) multiplexer_1 (
    .in0({_200_q, Counter}), .in1({_201_q, LED}), .in2({_202_q, TTY_out}), .in3({_203_q, clear, load_2}),
    .in4({{9{1'b0}}, keyboard_input}), .in5({{15{1'b0}}, button_status}), .out(out), .sel(Address[3:0]),
    .en(nor_1_out));  // open: in6, in7, in8, in9, in10, in11, in12, in13, in14, in15
  not not_2 (clk, En);
  Register #(.width(16), .trigger("falling")) _205 (
    .D(in), .en(decoder_1_out5), .Q({_205_q, En}), .clk(in_4));  // open: clr
endmodule

module test (
  input  in_1,
  input  [9:0] in_2,
  input  [15:0] in_3
);

  wire \i_o_컨트롤러_1_clear , \i_o_컨트롤러_1_load_2 , \i_o_컨트롤러_1_tty_clk ;
  wire [6:0] \i_o_컨트롤러_1_tty_out ;

  TTY #(.trigger("falling")) tty_1 (
    .data(\i_o_컨트롤러_1_tty_out ), .clk(\i_o_컨트롤러_1_tty_clk ), .we(\i_o_컨트롤러_1_load_2 ),
    .clr(\i_o_컨트롤러_1_clear ));
  \I_O_컨트롤러  \i_o_컨트롤러_1  (
    .Address(in_2), .in_4(in_1), .in(in_3), .TTY_out(\i_o_컨트롤러_1_tty_out ), .clear(\i_o_컨트롤러_1_clear ),
    .load_2(\i_o_컨트롤러_1_load_2 ), .tty_clk(\i_o_컨트롤러_1_tty_clk ));  // open: keyboard_input, clk, En, button_status, out, Counter, LED, Load
endmodule
